# Fritzing sketch circuit (saved by Fritzing 0.9.4)
breadboards: 1

parts:
  Part1 = Arduino Uno (Rev3)
  M1 = E18-D80NK_1 [package=THT]
  M2 = E18-D80NK_1 [package=THT]
  J1 = Basic Servo
  Part2 = LCD1602-I2C

nets:
  N1: Part1.D9_PWM, J1.pulse
  N2: Part1.A4/SDA, Part2.SDA
  N3: Part1.A5/SCL, Part2.SCL
  N4: Part1.D2, M1.pin3
  N5: Part1.D3_PWM, M2.pin3
  VCC: Part1.5V, M1.pin2, M2.pin2, J1.vcc, Part2.VCC
  GND: Part1.GND, M1.pin1, M2.pin1, J1.gnd, Part2.GND

custom parts:
  E18-D80NK_1: E18-D80NK Proximity Sensor module.
  LCD1602-I2C: A standard character display, usually with 2x16 characters. Comes in many colors with LCM1602 IIC attached.
