# Fritzing sketch cricuit (saved by Fritzing 0.9.4)

parts:
  U1 = ESP32-38PinWide [part_number=ESP32-38PinWide]  # not connected
  A1 = ESP32 devkit 38p expansion board
  LED1 = smd LED [color="Red (633nm)" package="1206 [SMD]"]
  LED2 = smd LED [color="Green (570nm)" package="1206 [SMD]"]
  M1 = fc-51 [package=THT]
  LED3 = smd LED [color="Red (633nm)" package="1206 [SMD]"]
  LED4 = smd LED [color="Green (570nm)" package="1206 [SMD]"]
  M2 = fc-51 [package=THT]
  LED5 = smd LED [color="Red (633nm)" package="1206 [SMD]"]
  LED6 = smd LED [color="Green (570nm)" package="1206 [SMD]"]
  M3 = fc-51 [package=THT]
  LED8 = smd LED [color="Green (570nm)" package="1206 [SMD]"]
  M4 = fc-51 [package=THT]
  LED7 = smd LED [color="Red (633nm)" package="1206 [SMD]"]
  M5 = E18-D80NK_1 [package=THT]
  M6 = E18-D80NK_1 [package=THT]
  J1 = Basic Servo
  Part1 = LCD1602-I2C

nets:
  N1: A1.Pin_4, M4.pin1
  N2: A1.Pin_5, M1.pin1
  N3: A1.Pin_6, M2.pin1
  N4: A1.Pin_7, M3.pin1
  N5: A1.Pin_9, J1.pulse
  N6: A1.Pin_10, LED5.anode
  N7: A1.Pin_11, M5.pin1
  N8: A1.Pin_13, M6.pin1
  N9: A1.Pin_18, A1.Pin_31, A1.Pin_146, A1.Pin_161, M4.pin3, M6.pin2, Part1.VCC
  N10: A1.Pin_35, A1.Pin_130, A1.Pin_144, LED8.cathode, M4.pin2, M5.pin3, Part1.GND
  N11: A1.Pin_117, A1.Pin_177, Part1.SCL
  N12: A1.Pin_168, LED3.anode
  N13: A1.Pin_169, LED1.anode
  N14: A1.Pin_170, LED6.anode
  N15: A1.Pin_171, LED4.anode
  N16: A1.Pin_172, LED2.anode
  N17: A1.Pin_173, LED8.anode
  N18: A1.Pin_174, Part1.SDA
  N19: A1.Pin_178, LED7.anode

custom parts:
  ESP32-38PinWide: Generic 38-Pin ESP32 with wide format (only access to one side of pins on a breadboard) based on Stephen Lilley's HiLetgo ESP-WROOM-32 ESP32 ESP-32S Development Board.
  ESP32 devkit 38p expansion board: Upgraded ESP32 38P Development ESP32-DevKitC-32 ESP-WROOM-32 Expansion Board.
  E18-D80NK_1: E18-D80NK Proximity Sensor module.
  LCD1602-I2C: A standard character display, usually with 2x16 characters. Comes in many colors with LCM1602 IIC attached.
