# Fritzing sketch circuit (saved by Fritzing 0.9.4)

parts:
  A1 = ESP32 devkit 38p expansion board
  U1 = ESP32-38PinWide [part_number=ESP32-38PinWide]  # not connected
  Part1 = LCD1602-I2C
  M1 = E18-D80NK_1 [package=THT]
  M2 = E18-D80NK_1 [package=THT]
  J1 = Basic Servo

nets:
  N1: A1.Pin_8, M1.pin3
  N2: A1.Pin_9, M2.pin3
  N3: A1.Pin_13, J1.pulse
  VCC: A1.Pin_18, A1.Pin_148, A1.Pin_156, A1.Pin_159, A1.Pin_161, Part1.VCC, M1.pin2, M2.pin2, J1.vcc
  GND: A1.Pin_35, A1.Pin_141, A1.Pin_143, A1.Pin_144, Part1.GND, M1.pin1, M2.pin1, J1.gnd
  N4: A1.Pin_174, Part1.SDA
  N5: A1.Pin_177, Part1.SCL

custom parts:
  ESP32 devkit 38p expansion board: Upgraded ESP32 38P Development ESP32-DevKitC-32 ESP-WROOM-32 Expansion Board.
  ESP32-38PinWide: Generic 38-Pin ESP32 with wide format (only access to one side of pins on a breadboard) based on Stephen Lilley's HiLetgo ESP-WROOM-32 ESP32 ESP-32S Development Board.
  LCD1602-I2C: A standard character display, usually with 2x16 characters. Comes in many colors with LCM1602 IIC attached.
  E18-D80NK_1: E18-D80NK Proximity Sensor module.
